# Fritzing sketch basic-traffic-light (saved by Fritzing 0.9.4)
breadboards: 1

parts:
  Part1 = Arduino Uno (Rev3)
  Red = LED - 5mm [color="Red (633nm)" package="5 mm [THT]"]
  R1 = Resistor [tolerance=±5% resistance=220 package=THT]
  Yellow = LED - 5mm [color="Yellow (595nm)" package="5 mm [THT]"]
  R2 = Resistor [tolerance=±5% resistance=220 package=THT]
  Green = LED - 5mm [color="Green (555nm)" package="5 mm [THT]"]
  R3 = Resistor [tolerance=±5% resistance=220 package=THT]

nets:
  N1: Part1.GND, R1.Pin_1, R2.Pin_1, R3.Pin_1
  N2: Part1.D3_PWM, Green.anode
  N3: Part1.D4, Yellow.anode
  N4: Part1.D5_PWM, Red.anode
  N5: Red.cathode, R1.Pin_0
  N6: Yellow.cathode, R2.Pin_0
  N7: Green.cathode, R3.Pin_0
